# Fritzing sketch circuitBoard (saved by Fritzing 0.9.6b)
breadboards: 1

parts:
  Part1 = Arduino Uno (Rev3)
  R1 = Resistor [tolerance=±5% power=0.25 resistance=10k package=THT]
  R2 = Resistor [tolerance=±5% power=0.25 resistance=220 package=THT]
  Q1 = TRANSISTOR_NPN [package=to-92-ammo]
  Q2 = Basic FET N-Channel [package="D2Pak [SMD]"]
  Part2 = Breakout Board for Electret Microphone

nets:
  N1: Part1.D9_PWM, R1.Pin_0
  N2: Part1.D3_PWM, Part2.AUD
  5V: Part1.5V, Part2.VCC
  N3: Part1.GND, Q1.C
  N4: Part1.VIN, R2.Pin_0, Q2.source
  N5: R1.Pin_1, Q1.B
  N6: R2.Pin_1, Q1.E, Q2.Gate

notes:
  connect this to your 12 V lEDs
  12 V DC
